// Logisim project poorten.circ as structural Verilog: 1 circuit, main circuit main
module main (
  input  in_1,
  input  in_2,
  input  in_3,
  input  in_4,
  input  in_5,
  input  in_6,
  input  in_7,
  input  in_8,
  input  in_9,
  input  in_10,
  output out_11,
  output out_12,
  output out_13,
  output out_14,
  output out_15,
  output out_16
);

  wire transistor_3_out;

  Pull_Resistor #(.pull(1)) pull_resistor_1 (.node(out_13));
  Transistor #(.\type ("n")) transistor_1 (.in(1'b0), .out(out_13), .gate(in_2));
  not not_1 (out_14, in_8);
  Pull_Resistor #(.pull(1)) pull_resistor_2 (.node(out_11));
  Transistor #(.\type ("n")) transistor_2 (.in(transistor_3_out), .out(out_11), .gate(in_1));
  Transistor #(.\type ("n")) transistor_3 (.in(1'b0), .out(transistor_3_out), .gate(in_5));
  nand nand_1 (out_15, in_6, in_9);
  Pull_Resistor #(.pull(1)) pull_resistor_3 (.node(out_12));
  Transistor #(.\type ("n")) transistor_4 (.in(1'b0), .out(out_12), .gate(in_3));
  Transistor #(.\type ("n")) transistor_5 (.in(1'b0), .out(out_12), .gate(in_4));
  nor nor_1 (out_16, in_7, in_10);

  // Notes on the sheet:
  //   NOT, NAND & NOR poorten met transistoren
endmodule
